# Fritzing sketch esp8266-dht22-mqtt (saved by Fritzing 0.9.3b)
breadboards: 2

parts:
  Gizwits_WiFi_Witty_ESP-12F1 = Gizwits WiFi Witty ESP-12F
  Bauteil1 = FTDI Basic Programmer
  R1 = Resistor [tolerance=±5% resistance=10k package=THT]
  R2 = Resistor [tolerance=±5% resistance=10k package=THT]
  RHT1 = Humidity and Temperature Sensor RHT03
  R3 = Resistor [tolerance=±5% resistance=10k package=THT]
  S1 = Pushbutton [package="[THT]"]
  R4 = Resistor [tolerance=±5% resistance=10k package=THT]
  VCC1 = Battery

nets:
  N1: Gizwits_WiFi_Witty_ESP-12F1.REST, R3.Pin_1, S1.Pin_3, S1.Pin_4
  N2: Gizwits_WiFi_Witty_ESP-12F1.CH_PD, R4.Pin_1
  VCC: Gizwits_WiFi_Witty_ESP-12F1.VCC, RHT1.Vcc, R3.Pin_0, R4.Pin_0, VCC1.+
  GND: Gizwits_WiFi_Witty_ESP-12F1.GND, Bauteil1.GND, R1.Pin_1, R2.Pin_1, RHT1.GND_2, S1.Pin_1, S1.Pin_2, VCC1.-
  N3: Gizwits_WiFi_Witty_ESP-12F1.GPIO15, R1.Pin_0
  N4: Gizwits_WiFi_Witty_ESP-12F1.GPIO0, R2.Pin_0
  N5: Gizwits_WiFi_Witty_ESP-12F1.GPIO4, RHT1.Data-signal
  N6: Gizwits_WiFi_Witty_ESP-12F1.RXD, Bauteil1.TXO
  N7: Gizwits_WiFi_Witty_ESP-12F1.TXD, Bauteil1.RXI

notes:
  # Connect GPIO0 to ground for flashing
  # Remove wire for normal operation
  RESET button to restart ESP8266 module
  USD to Serial Converter
